// Logisim project 16-bit Computer.circ as structural Verilog: 6 circuits, main circuit main
module main (
  input  Signed,
  input  [15:0] Bus_Override,
  input  in_3,
  input  [3:0] Op_Sel,
  input  Power,
  input  Manual_Override,
  input  in_7,
  input  in_8,
  input  in_9,
  input  in_10,
  input  in_11,
  input  in_12,
  input  in_13,
  input  in_14,
  input  in_15,
  input  in_16,
  input  in_17,
  output [3:0] out_18,
  output [15:0] out_19
);

  wire A_In, ALU_Out, AX_In, AX_Out, B_In, BP_In, BP_Out, button_1_out, button_2_out, button_3_out,
       button_4_out, button_5_out, button_6_out, button_7_out, button_8_out, button_9_out, button_10_out,
       button_11_out, button_12_out, button_13_out, BX_In, BX_Out, clock_1_out, comparator_1_eq,
       comparator_1_gt, comparator_1_lt, comparator_2_gt, comparator_2_lt, CX_In, CX_Out, decoder_1_out1,
       decoder_1_out2, decoder_1_out3, decoder_1_out4, decoder_1_out5, decoder_1_out6, decoder_1_out7,
       decoder_1_out8, decoder_1_out9, decoder_1_out10, DX_In, DX_Out, Halt, I_In, JA_out, JB_out, JE_out,
       JG_out, JL_out, JNA_out, JNB_out, JNE_out, JNG_out, JNL_out, Manual_Tick_out, MAR_In, not_1_out,
       not_2_out, not_3_out, not_4_out, not_5_out, not_6_out, or_23_out, PC_Inc, PC_Out, PC_Set, RAM_In,
       RAM_Out, Reset_Counter, SP_In, SP_Out;
  wire [3:0] I_q, I_q_2, I_q_3, I_q_4, or_1_out, or_7_out, or_7_out_2, rom_1_data, rom_1_data_2;
  wire [4:0] counter_1_q;
  wire [15:0] A_q, alu_1_alu_out, and_1_out, and_2_out, and_3_out, and_4_out, and_5_out, and_6_out,
       and_7_out, and_8_out, and_9_out, and_10_out, AX_q, B_q, BP_q, BX_q, CX_q, DX_q, MAR_q, or_8_out,
       or_29_out, ram_1_data, SP_q;
  wire [15:8] or_7_out_3;
  wire [19:0] rom_2_data;
  wire [31:20] rom_2_data_2;

  Hex_Digit_Display hex_digit_display_1 (.value(or_7_out_3[15:12]));  // open: dp
  Hex_Digit_Display hex_digit_display_2 (.value(or_7_out_2));  // open: dp
  Hex_Digit_Display hex_digit_display_3 (.value(or_7_out_3[11:8]));  // open: dp
  Button Manual_Tick (.out(Manual_Tick_out));
  _7_Segment_Display u_7_segment_display_1 ();  // open: g, f, a, b, e, d, c, dp
  Hex_Digit_Display hex_digit_display_4 (.value(or_7_out));  // open: dp
  assign and_1_out = Bus_Override & {16{in_3}};  // AND_Gate and_1, 16 bits wide
  assign or_1_out = Op_Sel | out_18;  // OR_Gate or_1, 4 bits wide
  Clock clock_1 (
    .Power(Power), .Manual_Override(Manual_Override), .Manual_Tick(Manual_Tick_out), .Halt(Halt),
    .Out(clock_1_out));
  or or_2 (AX_Out, rom_2_data[15], in_7);
  or or_3 (BX_Out, rom_2_data[16], in_11);
  or or_4 (CX_Out, rom_2_data[17], in_12);
  or or_5 (DX_Out, rom_2_data[18], in_14);
  or or_6 (Halt, rom_2_data[19], in_15);
  Hex_Digit_Display hex_digit_display_5 ();  // open: value, dp
  Hex_Digit_Display hex_digit_display_6 ();  // open: value, dp
  ALU alu_1 (.Operation(or_1_out), .A(A_q), .B(B_q), .ALU_Out(alu_1_alu_out));
  Register #(.width(16), .trigger("falling")) A (
    .D({or_7_out_3, or_7_out_2, or_7_out}), .Q(A_q), .clk(A_In));  // open: en, clr
  Register #(.width(16), .trigger("falling")) B (
    .D({or_7_out_3, or_7_out_2, or_7_out}), .Q(B_q), .clk(B_In));  // open: en, clr
  Register #(.width(16), .trigger("falling")) I (
    .D({or_7_out_3, or_7_out_2, or_7_out}), .Q({I_q_4, I_q_3, I_q_2, I_q}), .clk(I_In));  // open: en, clr
  Counter #(.width(5), .max('h12)) counter_1 (
    .Q(counter_1_q), .clk(clock_1_out), .clr(Reset_Counter));  // open: load, D, count, carry
  ROM #(.addrWidth(5)) rom_1 (.addr(counter_1_q), .data({rom_1_data, rom_1_data_2}));  // open: sel
  ROM #(.addrWidth(20), .dataWidth(32)) rom_2 (
    .addr({I_q_4, I_q_3, I_q_2, I_q, rom_1_data}),
    .data({rom_2_data_2[31:28], out_18, rom_2_data_2[23:20], rom_2_data}));  // open: sel
  Hex_Digit_Display hex_digit_display_7 ();  // open: value, dp
  Hex_Digit_Display hex_digit_display_8 ();  // open: value, dp
  assign {or_7_out_3, or_7_out_2, or_7_out} = and_1_out | and_7_out | and_2_out | and_8_out | or_8_out;  // OR_Gate or_7, 16 bits wide
  assign and_2_out = {16{ALU_Out}} & alu_1_alu_out;  // AND_Gate and_2, 16 bits wide
  Comparator #(.width(16), .mode("unsigned")) comparator_1 (
    .a(A_q), .b(B_q), .gt(comparator_1_gt), .eq(comparator_1_eq), .lt(comparator_1_lt));
  Comparator #(.width(16)) comparator_2 (.a(A_q), .b(B_q), .gt(comparator_2_gt), .lt(comparator_2_lt));  // open: eq
  not not_1 (not_1_out, comparator_2_lt);
  Button button_1 (.out(button_1_out));
  Button button_2 (.out(button_2_out));
  Button button_3 (.out(button_3_out));
  Button button_4 (.out(button_4_out));
  Hex_Digit_Display hex_digit_display_9 ();  // open: value, dp
  assign or_8_out = and_3_out | and_4_out | or_29_out | and_5_out | and_6_out;  // OR_Gate or_8, 16 bits wide
  not not_2 (not_2_out, comparator_1_gt);
  not not_3 (not_3_out, comparator_1_eq);
  not not_4 (not_4_out, comparator_1_lt);
  not not_5 (not_5_out, comparator_2_gt);
  Decoder #(.select(4), .disabled(0), .enable("false")) decoder_1 (
    .out1(decoder_1_out1), .out2(decoder_1_out2), .out3(decoder_1_out3), .out4(decoder_1_out4),
    .out5(decoder_1_out5), .out6(decoder_1_out6), .out7(decoder_1_out7), .out8(decoder_1_out8),
    .out9(decoder_1_out9), .out10(decoder_1_out10), .sel(rom_2_data_2[31:28]));  // open: out0, out11, out12, out13, out14, out15
  or or_9 (ALU_Out, rom_2_data[10], in_8);
  or or_10 (AX_In, rom_2_data[11], button_1_out);
  or or_11 (BX_In, rom_2_data[12], button_2_out);
  or or_12 (CX_In, rom_2_data[13], button_3_out);
  or or_13 (DX_In, rom_2_data[14], button_4_out);
  assign and_3_out = {16{DX_Out}} & DX_q;  // AND_Gate and_3, 16 bits wide
  Bin2Dec bin2dec_1 (
    .Input_Number({or_7_out_3, or_7_out_2, or_7_out}), .Signed(Signed));  // open: BCD_Output, Negative_Simbol
  assign and_4_out = {16{CX_Out}} & CX_q;  // AND_Gate and_4, 16 bits wide
  assign and_5_out = {16{BX_Out}} & BX_q;  // AND_Gate and_5, 16 bits wide
  assign and_6_out = {16{AX_Out}} & AX_q;  // AND_Gate and_6, 16 bits wide
  assign and_7_out = {16{PC_Out}} & out_19;  // AND_Gate and_7, 16 bits wide
  Register #(.width(16), .trigger("falling")) MAR (
    .D({or_7_out_3, or_7_out_2, or_7_out}), .Q(MAR_q), .clk(MAR_In));  // open: en, clr
  Register #(.width(16), .trigger("falling")) AX (
    .D({or_7_out_3, or_7_out_2, or_7_out}), .Q(AX_q), .clk(AX_In));  // open: en, clr
  PC pc_1 (.Set(PC_Set), .PC_Data({or_7_out_3, or_7_out_2, or_7_out}), .Increment(PC_Inc), .PC_Out(out_19));
  Button button_5 (.out(button_5_out));
  Button button_6 (.out(button_6_out));
  Button button_7 (.out(button_7_out));
  Button button_8 (.out(button_8_out));
  Button button_9 (.out(button_9_out));
  Button button_10 (.out(button_10_out));
  Register #(.width(16), .trigger("falling")) BX (
    .D({or_7_out_3, or_7_out_2, or_7_out}), .Q(BX_q), .clk(BX_In));  // open: en, clr
  assign and_8_out = {16{RAM_Out}} & ram_1_data;  // AND_Gate and_8, 16 bits wide
  RAM #(.addrWidth(16), .dataWidth(16), .bus("separate")) ram_1 (
    .addr(MAR_q), .din({or_7_out_3, or_7_out_2, or_7_out}), .data(ram_1_data), .clk(not_6_out));  // open: str, sel, ld, clr
  not not_6 (not_6_out, RAM_In);
  and JA (JA_out, comparator_1_gt, decoder_1_out1);
  and JNA (JNA_out, not_2_out, decoder_1_out2);
  and JE (JE_out, comparator_1_eq, decoder_1_out3);
  and JNE (JNE_out, not_3_out, decoder_1_out4);
  and JB (JB_out, comparator_1_lt, decoder_1_out5);
  and JNB (JNB_out, not_4_out, decoder_1_out6);
  and JG (JG_out, comparator_2_gt, decoder_1_out7);
  and JNG (JNG_out, not_5_out, decoder_1_out8);
  and JL (JL_out, comparator_2_lt, decoder_1_out9);
  and JNL (JNL_out, not_1_out, decoder_1_out10);
  or or_14 (PC_Set, rom_2_data[5], in_9);
  or or_15 (RAM_In, rom_2_data[6], button_5_out);
  or or_16 (Reset_Counter, rom_2_data[7], button_6_out);
  or or_17 (A_In, rom_2_data[8], button_7_out);
  or or_18 (B_In, rom_2_data[9], button_8_out);
  or or_19 (BP_Out, rom_2_data_2[20], in_16);
  or or_20 (BP_In, rom_2_data_2[21], button_9_out);
  or or_21 (SP_Out, rom_2_data_2[22], in_17);
  or or_22 (SP_In, rom_2_data_2[23], button_10_out);
  Register #(.width(16), .trigger("falling")) DX (
    .D({or_7_out_3, or_7_out_2, or_7_out}), .Q(DX_q), .clk(DX_In));  // open: en, clr
  Register #(.width(16), .trigger("falling")) CX (
    .D({or_7_out_3, or_7_out_2, or_7_out}), .Q(CX_q), .clk(CX_In));  // open: en, clr
  or or_23 (or_23_out, JA_out, JNA_out, JE_out, JNE_out, JB_out, JNB_out, JG_out, JNG_out, JL_out, JNL_out);
  Register #(.width(16), .trigger("falling")) BP (
    .D({or_7_out_3, or_7_out_2, or_7_out}), .Q(BP_q), .clk(BP_In));  // open: en, clr
  Register #(.width(16), .trigger("falling")) SP (
    .D({or_7_out_3, or_7_out_2, or_7_out}), .Q(SP_q), .clk(SP_In));  // open: en, clr
  Button button_11 (.out(button_11_out));
  Button button_12 (.out(button_12_out));
  Button button_13 (.out(button_13_out));
  assign and_9_out = BP_q & {16{BP_Out}};  // AND_Gate and_9, 16 bits wide
  assign and_10_out = SP_q & {16{SP_Out}};  // AND_Gate and_10, 16 bits wide
  or or_24 (PC_Out, rom_2_data[0], rom_1_data_2[0], in_10);
  or or_25 (MAR_In, rom_2_data[1], rom_1_data_2[1], button_11_out);
  or or_26 (RAM_Out, rom_2_data[2], rom_1_data_2[2], in_13);
  or or_27 (I_In, rom_2_data[3], rom_1_data_2[3], button_12_out);
  or or_28 (PC_Inc, rom_1_data_2[3], rom_2_data[4], button_13_out, or_23_out);
  assign or_29_out = and_9_out | and_10_out;  // OR_Gate or_29, 16 bits wide

  // Other names for the same wires on the sheet: Operation_Select[3:0] = out_18

  // Notes on the sheet:
  //   Micro Instructions
  //   Micro Controller
  //   contents of rom_1 (hex, n*v repeats v):
  //   0 3 c 0 10 20 30 40 50 60 70 80 90 a0 b0 c0 d0 e0 f0
  //   contents of rom_2 (hex, n*v repeats v):
  //   0 80 255*0 3 814 80 13*0 3 1014 80 13*0 3 2014 80 13*0 3 4014 80 13*0 3 200014 80 13*0 3 800014 80
  //   173*0 3 0 16 804 80 11*0 3 0 16 1004 80 11*0 3 0 16 2004 80 11*0 3 0 16 4004 80 11*0 3 0 16 200004
  //   80 11*0 3 0 16 800004 80 171*0 3 0 16 8040 80 11*0 3 0 16 10040 80 11*0 3 0 16 20040 80 11*0 3 0 16
  //   40040 80 11*0 3 0 16 100040 80 11*0 3 0 16 400040 80 171*0 3 8100 214 c00 80 11*0 3 10100 214 1400
  //   80 11*0 3 20100 214 2400 80 11*0 3 40100 214 4400 80 11*0 3 100100 214 200400 80 11*0 3 400100 214
  //   800400 80 171*0 3 8100 6 214 c00 80 10*0 3 10100 6 214 1400 80 10*0 3 20100 6 214 2400 80 10*0 3
  //   40100 6 214 4400 80 10*0 3 100100 6 214 200400 80 10*0 3 400100 6 214 800400 80 170*0 3 8200 6 114
  //   440 80 10*0 3 10200 6 114 440 80 10*0 3 20200 6 114 440 80 10*0 3 40200 6 114 440 80 10*0 3 100200 6
  //   114 440 80 10*0 3 400200 6 114 440 80 170*0 3 8100 214 1000c00 80 11*0 3 10100 214 1001400 80 11*0 3
  //   20100 214 1002400 80 11*0 3 40100 214 1004400 80 11*0 3 100100 214 1200400 80 11*0 3 400100 214
  //   1800400 80 171*0 3 8100 6 214 1000c00 80 10*0 3 10100 6 214 1001400 80 10*0 3 20100 6 214 1002400 80
  //   10*0 3 40100 6 214 1004400 80 10*0 3 100100 6 214 1200400 80 10*0 3 400100 6 214 1800400 80 170*0 3
  //   8200 6 114 1000440 80 10*0 3 10200 6 114 1000440 80 10*0 3 20200 6 114 1000440 80 10*0 3 40200 6 114
  //   1000440 80 10*0 3 100200 6 114 1000440 80 10*0 3 400200 6 114 1000440 80 170*0 3 8100 214 2000c00 80
  //   11*0 3 10100 214 2001400 80 11*0 3 20100 214 2002400 80 11*0 3 40100 214 2004400 80 11*0 3 100100
  //   214 2200400 80 11*0 3 400100 214 2800400 80 171*0 3 8100 6 214 2000c00 80 10*0 3 10100 6 214 2001400
  //   80 10*0 3 20100 6 214 2002400 80 10*0 3 40100 6 214 2004400 80 10*0 3 100100 6 214 2200400 80 10*0 3
  //   400100 6 214 2800400 80 170*0 3 8200 6 114 2000440 80 10*0 3 10200 6 114 2000440 80 10*0 3 20200 6
  //   114 2000440 80 10*0 3 40200 6 114 2000440 80 10*0 3 100200 6 114 2000440 80 10*0 3 400200 6 114
  //   2000440 80 170*0 3 8100 214 3000c00 80 11*0 3 10100 214 3001400 80 11*0 3 20100 214 3002400 80 11*0
  //   3 40100 214 3004400 80 11*0 3 100100 214 3200400 80 11*0 3 400100 214 3800400 80 171*0 3 8100 6 214
  //   3000c00 80 10*0 3 10100 6 214 3001400 80 10*0 3 20100 6 214 3002400 80 10*0 3 40100 6 214 3004400 80
  //   10*0 3 100100 6 214 3200400 80 10*0 3 400100 6 214 3800400 80 170*0 3 8200 6 114 3000440 80 10*0 3
  //   10200 6 114 3000440 80 10*0 3 20200 6 114 3000440 80 10*0 3 40200 6 114 3000440 80 10*0 3 100200 6
  //   114 3000440 80 10*0 3 400200 6 114 3000440 80 170*0 8800 80 14*0 10800 80 14*0 20800 80 14*0 40800
  //   80 14*0 100800 80 14*0 400800 80 174*0 9000 80 14*0 11000 80 14*0 21000 80 14*0 41000 80 14*0 101000
  //   80 14*0 401000 80 174*0 a000 80 14*0 12000 80 14*0 22000 80 14*0 42000 80 14*0 102000 80 14*0 402000
  //   80 174*0 c000 80 14*0 14000 80 14*0 24000 80 14*0 44000 80 14*0 104000 80 14*0 404000 80 174*0
  //   208000 80 14*0 210000 80 14*0 220000 80 14*0 240000 80 14*0 300000 80 14*0 600000 80 174*0 808000 80
  //   14*0 810000 80 14*0 820000 80 14*0 840000 80 14*0 900000 80 14*0 c00000 80 2734*0 8002 804 80 13*0
  //   10002 804 80 13*0 20002 804 80 13*0 40002 804 80 13*0 100002 804 80 13*0 400002 804 80 173*0 8002
  //   1004 80 13*0 10002 1004 80 13*0 20002 1004 80 13*0 40002 1004 80 13*0 100002 1004 80 13*0 400002
  //   1004 80 173*0 8002 2004 80 13*0 10002 2004 80 13*0 20002 2004 80 13*0 40002 2004 80 13*0 100002 2004
  //   80 13*0 400002 2004 80 173*0 8002 4004 80 13*0 10002 4004 80 13*0 20002 4004 80 13*0 40002 4004 80
  //   13*0 100002 4004 80 13*0 400002 4004 80 173*0 8002 200004 80 13*0 10002 200004 80 13*0 20002 200004
  //   80 13*0 40002 200004 80 13*0 100002 200004 80 13*0 400002 200004 80 173*0 8002 800004 80 13*0 10002
  //   800004 80 13*0 20002 800004 80 13*0 40002 800004 80 13*0 100002 800004 80 13*0 400002 800004 80
  //   2733*0 8002 8040 80 13*0 8002 10040 80 29*0 8002 40040 80 13*0 8002 100040 80 13*0 8002 400040 80
  //   173*0 10002 8040 80 13*0 10002 10040 80 29*0 10002 40040 80 13*0 10002 100040 80 13*0 10002 400040
  //   80 173*0 20002 8040 80 13*0 20002 10040 80 29*0 20002 40040 80 13*0 20002 100040 80 13*0 20002
  //   400040 80 173*0 40002 8040 80 13*0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
  //   RAM
endmodule

module Clock (
  input  Power,
  input  Manual_Override,
  input  Manual_Tick,
  input  Halt,
  output Out
);

  wire and_1_out, and_2_out, clock_1_out, not_1_out, not_2_out, or_1_out;

  Clock_part clock_1 (.out(clock_1_out));
  not not_1 (not_1_out, Manual_Override);
  and and_1 (and_1_out, not_1_out, clock_1_out);
  and and_2 (and_2_out, Manual_Override, Manual_Tick);
  or or_1 (or_1_out, and_1_out, and_2_out);
  not not_2 (not_2_out, Halt);
  and and_3 (Out, Power, not_2_out, or_1_out);
endmodule

module ALU (
  input  [3:0] Operation,
  input  [15:0] A,
  input  [15:0] B,
  output [15:0] ALU_Out
);

  wire [15:0] adder_1_out, adder_2_out, and_1_out, divider_1_out, multiplier_1_out, negator_1_out, not_1_out,
       or_1_out, shifter_1_out, shifter_2_out, shifter_3_out, shifter_4_out, shifter_5_out, subtractor_1_out,
       subtractor_2_out, xor_1_out;

  Adder #(.width(16)) adder_1 (.a(A), .b(B), .out(adder_1_out));  // open: cin, cout
  Subtractor #(.width(16)) subtractor_1 (.a(A), .b(B), .out(subtractor_1_out));  // open: bin, bout
  Multiplier #(.width(16)) multiplier_1 (.a(A), .b(B), .out(multiplier_1_out));  // open: cin, cout
  Divider #(.width(16)) divider_1 (.a(A), .b(B), .out(divider_1_out));  // open: upper, rem
  Shifter #(.width(16)) shifter_1 (.in(A), .\dist (B[3:0]), .out(shifter_1_out));
  Shifter #(.width(16), .shift("lr")) shifter_2 (.in(A), .\dist (B[3:0]), .out(shifter_2_out));
  Shifter #(.width(16), .shift("ar")) shifter_3 (.in(A), .\dist (B[3:0]), .out(shifter_3_out));
  Shifter #(.width(16), .shift("rl")) shifter_4 (.in(A), .\dist (B[3:0]), .out(shifter_4_out));
  Shifter #(.width(16), .shift("rr")) shifter_5 (.in(A), .\dist (B[3:0]), .out(shifter_5_out));
  assign and_1_out = A & B;  // AND_Gate and_1, 16 bits wide
  assign or_1_out = A | B;  // OR_Gate or_1, 16 bits wide
  assign xor_1_out = A ^ B;  // XOR_Gate xor_1, 16 bits wide
  assign not_1_out = ~A;  // NOT_Gate not_1, 16 bits wide
  Negator #(.width(16)) negator_1 (.in(A), .out(negator_1_out));
  Adder #(.width(16)) adder_2 (.a(A), .b(16'h1), .out(adder_2_out));  // open: cin, cout
  Subtractor #(.width(16)) subtractor_2 (.a(A), .b(16'h1), .out(subtractor_2_out));  // open: bin, bout
  Multiplexer #(.select(4), .width(16), .disabled(0), .enable("false")) multiplexer_1 (
    .in0(adder_1_out), .in1(subtractor_1_out), .in2(multiplier_1_out), .in3(divider_1_out),
    .in4(shifter_1_out), .in5(shifter_2_out), .in6(shifter_3_out), .in7(shifter_4_out), .in8(shifter_5_out),
    .in9(and_1_out), .in10(or_1_out), .in11(xor_1_out), .in12(not_1_out), .in13(negator_1_out),
    .in14(adder_2_out), .in15(subtractor_2_out), .out(ALU_Out), .sel(Operation));
endmodule

module PC (
  input  Set,
  input  [15:0] PC_Data,
  input  Increment,
  output [15:0] PC_Out
);

  wire or_1_out;
  wire [15:0] adder_1_out, multiplexer_1_out;

  Adder #(.width(16)) adder_1 (.a(PC_Out), .b(16'h1), .out(adder_1_out));  // open: cin, cout
  Multiplexer #(.width(16), .disabled(0), .enable("false")) multiplexer_1 (
    .in0(adder_1_out), .in1(PC_Data), .out(multiplexer_1_out), .sel(Set));
  or or_1 (or_1_out, Set, Increment);
  Register #(.width(16), .trigger("falling")) register_1 (
    .D(multiplexer_1_out), .Q(PC_Out), .clk(or_1_out));  // open: en, clr
endmodule

// B2D
module Bin2Dec (
  input  Negative_Simbol,
  input  Signed,
  input  [15:0] Input_Number,
  output [19:0] BCD_Output
);

  wire undriven, undriven_2, undriven_3, undriven_4, undriven_5, undriven_6, undriven_7, undriven_8,
       undriven_9, undriven_10, undriven_11, undriven_12, undriven_13, undriven_14, undriven_15, undriven_16,
       undriven_17, undriven_18, undriven_19, undriven_20, undriven_21, undriven_22, undriven_23,
       undriven_24, undriven_25, undriven_26, undriven_27, undriven_28, undriven_29, undriven_30,
       undriven_31, undriven_32, undriven_33, undriven_34, undriven_35, undriven_36, undriven_37,
       undriven_38, undriven_39, undriven_40, undriven_41, undriven_42;

  Bin2Dec_add3 bin2dec_add3_1 (
    .in_1(BCD_Output[18]), .in_2(BCD_Output[17]), .in_3(BCD_Output[16]), .in_4(BCD_Output[15]), .in_5(1'b0),
    .in_6(undriven), .in_7(undriven_2), .in_8(undriven_4));
  Bin2Dec_add3 bin2dec_add3_2 (
    .in_1(undriven), .in_2(undriven_2), .in_3(undriven_4), .in_4(BCD_Output[14]), .in_5(1'b0),
    .in_6(undriven_3), .in_7(undriven_5), .in_8(undriven_7));
  Bin2Dec_add3 bin2dec_add3_3 (
    .in_1(undriven_3), .in_2(undriven_5), .in_3(undriven_7), .in_4(BCD_Output[13]), .in_5(1'b0),
    .in_6(undriven_6), .in_7(undriven_8), .in_8(undriven_10));
  Bin2Dec_add3 bin2dec_add3_4 (
    .in_1(undriven_6), .in_2(undriven_8), .in_3(undriven_10), .in_4(BCD_Output[12]), .in_5(Input_Number[15]),
    .in_6(undriven_9), .in_7(undriven_11), .in_8(undriven_13));
  Bin2Dec_add3 bin2dec_add3_5 (
    .in_1(undriven_9), .in_2(undriven_11), .in_3(undriven_13), .in_4(BCD_Output[11]),
    .in_5(Input_Number[14]), .in_6(undriven_12), .in_7(undriven_14), .in_8(undriven_16));
  Bin2Dec_add3 bin2dec_add3_6 (
    .in_1(undriven_12), .in_2(undriven_14), .in_3(undriven_16), .in_4(BCD_Output[10]),
    .in_5(Input_Number[13]), .in_6(undriven_15), .in_7(undriven_17), .in_8(undriven_19));
  Bin2Dec_add3 bin2dec_add3_7 (
    .in_1(undriven_15), .in_2(undriven_17), .in_3(undriven_19), .in_4(BCD_Output[9]),
    .in_5(Input_Number[12]), .in_6(undriven_18), .in_7(undriven_20), .in_8(undriven_22));
  Bin2Dec_add3 bin2dec_add3_8 (
    .in_1(undriven_18), .in_2(undriven_20), .in_3(undriven_22), .in_4(BCD_Output[8]),
    .in_5(Input_Number[11]), .in_6(undriven_21), .in_7(undriven_23), .in_8(undriven_25));
  Bin2Dec_add3 bin2dec_add3_9 (
    .in_1(undriven_21), .in_2(undriven_23), .in_3(undriven_25), .in_4(BCD_Output[7]),
    .in_5(Input_Number[10]), .in_6(undriven_24), .in_7(undriven_26), .in_8(undriven_28));
  Bin2Dec_add3 bin2dec_add3_10 (
    .in_1(undriven_24), .in_2(undriven_26), .in_3(undriven_28), .in_4(BCD_Output[6]), .in_5(Input_Number[9]),
    .in_6(undriven_27), .in_7(undriven_29), .in_8(undriven_31));
  Bin2Dec_add3 bin2dec_add3_11 (
    .in_1(undriven_27), .in_2(undriven_29), .in_3(undriven_31), .in_4(BCD_Output[5]), .in_5(Input_Number[8]),
    .in_6(undriven_30), .in_7(undriven_32), .in_8(undriven_34));
  Bin2Dec_add3 bin2dec_add3_12 (
    .in_1(undriven_30), .in_2(undriven_32), .in_3(undriven_34), .in_4(BCD_Output[4]), .in_5(Input_Number[7]),
    .in_6(undriven_33), .in_7(undriven_35), .in_8(undriven_37));
  Bin2Dec_add3 bin2dec_add3_13 (
    .in_1(undriven_33), .in_2(undriven_35), .in_3(undriven_37), .in_4(BCD_Output[3]), .in_5(Input_Number[6]),
    .in_6(undriven_36), .in_7(undriven_38), .in_8(undriven_40));
  Bin2Dec_add3 bin2dec_add3_14 (
    .in_1(undriven_36), .in_2(undriven_38), .in_3(undriven_40), .in_4(BCD_Output[2]), .in_5(Input_Number[5]),
    .in_6(undriven_39), .in_7(undriven_41), .in_8(undriven_42));
  and and_1 (Negative_Simbol, Input_Number[15], Signed);
  Bin2Dec_add3 bin2dec_add3_15 (
    .in_1(undriven_39), .in_2(undriven_41), .in_3(undriven_42), .in_4(BCD_Output[1]), .in_5(Input_Number[4]),
    .in_6(Input_Number[3]), .in_7(Input_Number[2]), .in_8(Input_Number[1]));

  assign {BCD_Output[19], BCD_Output[0]} = {1'b0, Input_Number[0]};
endmodule

// Add3
module Bin2Dec_add3 (
  input  in_1,
  input  in_2,
  input  in_3,
  input  in_4,
  input  in_5,
  input  in_6,
  input  in_7,
  input  in_8
);

  ROM #(.addrWidth(4), .dataWidth(4)) rom_1 (
    .addr({in_5, in_6, in_7, in_8}), .data({in_1, in_2, in_3, in_4}));  // open: sel

  // Notes on the sheet:
  //   contents of rom_1 (hex, n*v repeats v):
  //   0 1 2 3 4 8 9 a b c 6*e
endmodule
